// Logisim project I-Type instruction.circ as structural Verilog: 5 circuits, main circuit main
module main (
  input  MemWrite,
  input  MemRead,
  input  Clear,
  input  RegWrite,
  input  Clock,
  output [15:0] Data,
  output [15:0] out_7,
  output [1:0] out_8,
  output [15:0] Data_2,
  output [15:0] out_10,
  output [15:0] out_11,
  output [15:0] out_12
);

  wire [1:0] adder_1_out, bit_extender_2_out, register_1_q;

  Register #(.width(2)) register_1 (.D(adder_1_out), .Q(register_1_q), .clk(Clock), .clr(Clear));  // open: en
  Adder #(.width(2)) adder_1 (.a(2'b01), .b(register_1_q), .out(adder_1_out));  // open: cin, cout
  ROM #(.addrWidth(2), .dataWidth(16)) rom_1 (.addr(register_1_q), .data(Data));  // open: sel
  assign out_12 = {{12{1'b0}}, Data[3:0]};  // Bit_Extender bit_extender_1
  Bit_Extender #(.in_width(4), .out_width(2)) bit_extender_2 (.in(Data[15:12]), .out(bit_extender_2_out));
  _16_Bit_Register Register_2 (
    .Read_Register_1(Data[11:8]), .Read_Regiter_2(Data[7:4]), .Write_Data(out_10), .RegWrite(RegWrite),
    .CLK(Clock), .Read_Data_1(out_11), .Read_Data_2(Data_2));  // open: Write_Register
  Bit_Extender #(.in_width(16), .out_width(2)) bit_extender_3 (.in(out_7), .out(out_8));
  _16_Bit_ALU ALU (
    .A(out_11), .B(out_12), .Operand(bit_extender_2_out), .Result(out_7));  // open: Binvert, Carryin, Zero, Overflow, CarryOut
  RAM #(.addrWidth(2), .dataWidth(16), .bus("separate")) ram_1 (
    .addr(out_8), .din(out_10), .data(Data_2), .str(MemWrite), .clk(Clock), .ld(MemRead));  // open: sel, clr
endmodule

module Rigister_file (
  input  [1:0] Write_Register__RD,
  input  [1:0] Read_Reagister_1__RS,
  input  [1:0] Read_Reagister_2__RT,
  input  [15:0] Write_Data,
  input  RegWrite,
  input  CLK,
  output [15:0] Read_Data_1,
  output [15:0] Read_Data_2
);

  wire and_1_out, and_2_out, and_3_out, and_4_out, decoder_1_out0, decoder_1_out1, decoder_1_out2,
       decoder_1_out3;
  wire [15:0] _0_q, _1_q, _2_q, _3_q;

  Decoder #(.select(2)) decoder_1 (
    .out0(decoder_1_out0), .out1(decoder_1_out1), .out2(decoder_1_out2), .out3(decoder_1_out3),
    .sel(Write_Register__RD));  // open: en
  and and_1 (and_1_out, decoder_1_out0, RegWrite);
  and and_2 (and_2_out, decoder_1_out1, RegWrite);
  and and_3 (and_3_out, decoder_1_out2, RegWrite);
  and and_4 (and_4_out, decoder_1_out3, RegWrite);
  Register #(.width(16)) _0 (.D(Write_Data), .en(and_1_out), .Q(_0_q), .clk(CLK));  // open: clr
  Register #(.width(16)) _1 (.D(Write_Data), .en(and_2_out), .Q(_1_q), .clk(CLK));  // open: clr
  Register #(.width(16)) _2 (.D(Write_Data), .en(and_3_out), .Q(_2_q), .clk(CLK));  // open: clr
  Register #(.width(16)) _3 (.D(Write_Data), .en(and_4_out), .Q(_3_q), .clk(CLK));  // open: clr
  Multiplexer #(.select(2), .width(16)) multiplexer_1 (
    .in0(_0_q), .in1(_1_q), .in2(_2_q), .in3(_3_q), .out(Read_Data_1), .sel(Read_Reagister_1__RS));  // open: en
  Multiplexer #(.select(2), .width(16)) multiplexer_2 (
    .in0(_0_q), .in1(_1_q), .in2(_2_q), .in3(_3_q), .out(Read_Data_2), .sel(Read_Reagister_2__RT));  // open: en
endmodule

module ALU (
  input  B,
  input  A,
  input  Carry_in,
  input  [1:0] Operand,
  input  Binvert,
  output Result,
  output CarryOut
);

  wire adder_1_out, and_1_out, multiplexer_1_out, not_1_out, or_1_out;

  not not_1 (not_1_out, B);
  Multiplexer multiplexer_1 (.in0(not_1_out), .in1(B), .out(multiplexer_1_out), .sel(Binvert));  // open: en
  and and_1 (and_1_out, A, multiplexer_1_out);
  or or_1 (or_1_out, A, multiplexer_1_out);
  Adder #(.width(1)) adder_1 (.a(A), .b(multiplexer_1_out), .out(adder_1_out), .cin(Carry_in), .cout(CarryOut));
  Multiplexer #(.select(2)) multiplexer_2 (
    .in0(and_1_out), .in1(or_1_out), .in2(adder_1_out), .out(Result), .sel(Operand));  // open: in3, en
endmodule

module _16_Bit_Register (
  input  [3:0] Read_Register_1,
  input  [3:0] Read_Regiter_2,
  input  [3:0] Write_Register,
  input  [15:0] Write_Data,
  input  RegWrite,
  input  CLK,
  output [15:0] Read_Data_1,
  output [15:0] Read_Data_2
);

  wire and_1_out, and_2_out, and_3_out, and_4_out, and_5_out, and_6_out, and_7_out, and_8_out, and_9_out,
       and_10_out, and_11_out, and_12_out, and_13_out, and_14_out, and_15_out, and_16_out, decoder_1_out0,
       decoder_1_out1, decoder_1_out2, decoder_1_out3, decoder_1_out4, decoder_1_out5, decoder_1_out6,
       decoder_1_out7, decoder_1_out8, decoder_1_out10, decoder_1_out11, decoder_1_out12, decoder_1_out13,
       decoder_1_out14, decoder_1_out15;
  wire [15:0] register_1_q, register_2_q, register_3_q, register_4_q, register_5_q, register_6_q,
       register_7_q, register_8_q, register_9_q, register_10_q, register_11_q, register_12_q, register_13_q,
       register_14_q, register_15_q, register_16_q;

  Decoder #(.select(4)) decoder_1 (
    .out0(decoder_1_out0), .out1(decoder_1_out1), .out2(decoder_1_out2), .out3(decoder_1_out3),
    .out4(decoder_1_out4), .out5(decoder_1_out5), .out6(decoder_1_out6), .out7(decoder_1_out7),
    .out8(decoder_1_out8), .out9(decoder_1_out8), .out10(decoder_1_out10), .out11(decoder_1_out11),
    .out12(decoder_1_out12), .out13(decoder_1_out13), .out14(decoder_1_out14), .out15(decoder_1_out15),
    .sel(Write_Register));  // open: en
  and and_1 (and_1_out, decoder_1_out0, RegWrite);
  and and_2 (and_2_out, decoder_1_out1, RegWrite);
  and and_3 (and_3_out, decoder_1_out2, RegWrite);
  and and_4 (and_4_out, decoder_1_out3, RegWrite);
  and and_5 (and_5_out, decoder_1_out4, RegWrite);
  and and_6 (and_6_out, decoder_1_out5, RegWrite);
  and and_7 (and_7_out, decoder_1_out6, RegWrite);
  and and_8 (and_8_out, decoder_1_out7, RegWrite);
  Register #(.width(16)) register_1 (.D(Write_Data), .Q(register_1_q), .clk(CLK), .clr(and_1_out));  // open: en
  Register #(.width(16)) register_2 (.D(Write_Data), .Q(register_2_q), .clk(CLK), .clr(and_2_out));  // open: en
  Register #(.width(16)) register_3 (.D(Write_Data), .Q(register_3_q), .clk(CLK), .clr(and_3_out));  // open: en
  Register #(.width(16)) register_4 (.D(Write_Data), .Q(register_4_q), .clk(CLK), .clr(and_4_out));  // open: en
  Register #(.width(16)) register_5 (.D(Write_Data), .Q(register_5_q), .clk(CLK), .clr(and_5_out));  // open: en
  Register #(.width(16)) register_6 (.D(Write_Data), .Q(register_6_q), .clk(CLK), .clr(and_6_out));  // open: en
  Register #(.width(16)) register_7 (.D(Write_Data), .Q(register_7_q), .clk(CLK), .clr(and_7_out));  // open: en
  Register #(.width(16)) register_8 (.D(Write_Data), .Q(register_8_q), .clk(CLK), .clr(and_8_out));  // open: en
  and and_9 (and_9_out, decoder_1_out8, RegWrite);
  and and_10 (and_10_out, decoder_1_out8, RegWrite);
  and and_11 (and_11_out, decoder_1_out10, RegWrite);
  and and_12 (and_12_out, decoder_1_out11, RegWrite);
  and and_13 (and_13_out, decoder_1_out12, RegWrite);
  and and_14 (and_14_out, decoder_1_out13, RegWrite);
  and and_15 (and_15_out, decoder_1_out14, RegWrite);
  and and_16 (and_16_out, decoder_1_out15, RegWrite);
  Register #(.width(16)) register_9 (.D(Write_Data), .Q(register_9_q), .clk(CLK), .clr(and_9_out));  // open: en
  Register #(.width(16)) register_10 (.D(Write_Data), .Q(register_10_q), .clk(CLK), .clr(and_10_out));  // open: en
  Register #(.width(16)) register_11 (.D(Write_Data), .Q(register_11_q), .clk(CLK), .clr(and_11_out));  // open: en
  Register #(.width(16)) register_12 (.D(Write_Data), .Q(register_12_q), .clk(CLK), .clr(and_12_out));  // open: en
  Register #(.width(16)) register_13 (.D(Write_Data), .Q(register_13_q), .clk(CLK), .clr(and_13_out));  // open: en
  Register #(.width(16)) register_14 (.D(Write_Data), .Q(register_14_q), .clk(CLK), .clr(and_14_out));  // open: en
  Register #(.width(16)) register_15 (.D(Write_Data), .Q(register_15_q), .clk(CLK), .clr(and_15_out));  // open: en
  Register #(.width(16)) register_16 (.D(Write_Data), .Q(register_16_q), .clk(CLK), .clr(and_16_out));  // open: en
  Multiplexer #(.select(4), .width(16)) multiplexer_1 (
    .in0(register_1_q), .in1(register_2_q), .in2(register_3_q), .in3(register_4_q), .in4(register_5_q),
    .in5(register_6_q), .in6(register_7_q), .in7(register_8_q), .in8(register_9_q), .in9(register_10_q),
    .in10(register_11_q), .in11(register_12_q), .in12(register_13_q), .in13(register_14_q),
    .in14(register_15_q), .in15(register_16_q), .out(Read_Data_1), .sel(Read_Register_1));  // open: en
  Multiplexer #(.select(4), .width(16)) multiplexer_2 (
    .in0(register_1_q), .in1(register_2_q), .in2(register_3_q), .in3(register_4_q), .in4(register_5_q),
    .in5(register_6_q), .in6(register_7_q), .in7(register_8_q), .in8(register_9_q), .in9(register_10_q),
    .in10(register_11_q), .in11(register_12_q), .in12(register_13_q), .in13(register_14_q),
    .in14(register_15_q), .in15(register_16_q), .out(Read_Data_2), .sel(Read_Regiter_2));  // open: en
endmodule

module _16_Bit_ALU (
  input  Carryin,
  input  [15:0] A,
  input  [15:0] B,
  input  [15:0] Result,
  input  Binvert,
  input  [1:0] Operand,
  output Zero,
  output Overflow,
  output CarryOut
);

  wire alu_1_carryout, alu_2_carryout, alu_3_carryout, alu_4_carryout, alu_5_carryout, alu_6_carryout,
       alu_7_carryout, alu_8_carryout, alu_9_carryout, alu_10_carryout, alu_11_carryout, alu_12_carryout,
       alu_13_carryout, alu_14_carryout, alu_15_carryout;

  ALU alu_1 (
    .Result(Result[0]), .CarryOut(alu_1_carryout), .B(B[0]), .A(A[0]), .Carry_in(Carryin), .Binvert(Binvert),
    .Operand(Operand));
  ALU alu_2 (
    .Result(Result[1]), .CarryOut(alu_2_carryout), .B(B[1]), .A(A[1]), .Carry_in(alu_1_carryout),
    .Binvert(Binvert), .Operand(Operand));
  ALU alu_3 (
    .Result(Result[2]), .CarryOut(alu_3_carryout), .B(B[2]), .A(A[2]), .Carry_in(alu_2_carryout),
    .Binvert(Binvert), .Operand(Operand));
  ALU alu_4 (
    .Result(Result[3]), .CarryOut(alu_4_carryout), .B(B[3]), .A(A[3]), .Carry_in(alu_3_carryout),
    .Binvert(Binvert), .Operand(Operand));
  ALU alu_5 (
    .Result(Result[4]), .CarryOut(alu_5_carryout), .B(B[4]), .A(A[4]), .Carry_in(alu_4_carryout),
    .Binvert(Binvert), .Operand(Operand));
  ALU alu_6 (
    .Result(Result[5]), .CarryOut(alu_6_carryout), .B(B[5]), .A(A[5]), .Carry_in(alu_5_carryout),
    .Binvert(Binvert), .Operand(Operand));
  ALU alu_7 (
    .Result(Result[6]), .CarryOut(alu_7_carryout), .B(B[6]), .A(A[6]), .Carry_in(alu_6_carryout),
    .Binvert(Binvert), .Operand(Operand));
  ALU alu_8 (
    .Result(Result[7]), .CarryOut(alu_8_carryout), .B(B[7]), .A(A[7]), .Carry_in(alu_7_carryout),
    .Binvert(Binvert), .Operand(Operand));
  ALU alu_9 (
    .Result(Result[8]), .CarryOut(alu_9_carryout), .B(B[8]), .A(A[8]), .Carry_in(alu_8_carryout),
    .Binvert(Binvert), .Operand(Operand));
  ALU alu_10 (
    .Result(Result[9]), .CarryOut(alu_10_carryout), .B(B[9]), .A(A[9]), .Carry_in(alu_9_carryout),
    .Binvert(Binvert), .Operand(Operand));
  ALU alu_11 (
    .Result(Result[10]), .CarryOut(alu_11_carryout), .B(B[10]), .A(A[10]), .Carry_in(alu_10_carryout),
    .Binvert(Binvert), .Operand(Operand));
  ALU alu_12 (
    .Result(Result[11]), .CarryOut(alu_12_carryout), .B(B[11]), .A(A[11]), .Carry_in(alu_11_carryout),
    .Binvert(Binvert), .Operand(Operand));
  ALU alu_13 (
    .Result(Result[12]), .CarryOut(alu_13_carryout), .B(B[12]), .A(A[12]), .Carry_in(alu_12_carryout),
    .Binvert(Binvert), .Operand(Operand));
  ALU alu_14 (
    .Result(Result[13]), .CarryOut(alu_14_carryout), .B(B[13]), .A(A[13]), .Carry_in(alu_13_carryout),
    .Binvert(Binvert), .Operand(Operand));
  ALU alu_15 (
    .Result(Result[14]), .CarryOut(alu_15_carryout), .B(B[14]), .A(A[14]), .Carry_in(alu_14_carryout),
    .Binvert(Binvert), .Operand(Operand));
  ALU alu_16 (
    .Result(Result[15]), .CarryOut(CarryOut), .B(B[14]), .A(A[14]), .Carry_in(alu_15_carryout),
    .Binvert(Binvert), .Operand(Operand));
  xnor xnor_1 (Overflow, CarryOut, CarryOut);
  nor nor_1 (Zero, Result[0], Result[1], Result[2], Result[3], Result[4], Result[5], Result[6], Result[7], Result[8], Result[9], Result[10], Result[11], Result[12], Result[13], Result[14], Result[15]);
endmodule
